# Fritzing sketch LED_Photores_Attiny85 (saved by Fritzing 0.9.3b)
circuit board: 8.46667cm x 5.64444cm
breadboards: 1

parts:
  U1 = attiny85 [package=dip]
  LED1 = LED - 5mm [color="Red (633nm)" package="5 mm [THT]"]
  R1 = Photocell (LDR) [package=THT]
  Часть1 = LilyPad Coin Cell Battery Holder
  R2 = Resistor [tolerance=±5% resistance=220 package=THT]
  R3 = Resistor [tolerance=±5% resistance=10k package=THT]

nets:
  N1: U1.Pin_4, LED1.cathode, R1.pin_1, Часть1.-
  N2: U1.Pin_5, R2.Pin_1
  N3: U1.Pin_7, R1.pin_0, R3.Pin_1
  N4: U1.Pin_8, Часть1.+, R3.Pin_0
  N5: LED1.anode, R2.Pin_0
